# Fritzing sketch schematic (saved by Fritzing 1.0.6)
breadboards: 1

parts:
  M1 = >Wemos D1 R32
  Part1 = Current Sensor 5A
  A1 = four channel mosfet switch
  F1 = Fan - Ventilador [package=THT]
  A2 = COB 12V LED strip
  A3 = COB 12V LED strip  # not connected
  A4 = COB 12V LED strip  # not connected
  Grove1 = Grove OLED 128x96
  M2 = fc-51 [package=THT]
  M3 = fc-51 [package=THT]
  A5 = 100w-ptc-air-heater
  Adaptor_12V = 2.1mm Barrel Jack with Terminal Block
  R1 = Resistor [tolerance=±5% resistance=10k package="2512 [SMD]"]
  R2 = Photocell (LDR) [power=0.25W dark_resistance_@0.01lx=300kΩ light_resistance_@100lx=400Ω luminance=10lx package=THT]
  DHT2 = DHT11 Humitidy and Temperature Sensor (3 pins)
  R3 = Resistor [tolerance=±5% resistance=10k package="2512 [SMD]"]
  R4 = Resistor [tolerance=±5% resistance=10k package="2512 [SMD]"]
  R5 = Resistor [tolerance=±5% resistance=10k package="2512 [SMD]"]
  F2 = Fan - Ventilador [package=THT]
  Part2 = INMP441
  S1 = Pushbutton [package="[SMD]"]

nets:
  5V: M1.5V, Part1.VCC, A1.CH3_+, A1.CH2_+, A1.CH1_+
  3V3: M1.3V3, Grove1.VCC, M2.pin3, M3.pin3, R2.pin_0, DHT2.Plus, Part2.VDD
  GND: M1.GND, Part1.GND, A1.M1_-, A1.M2_-, A1.M3_-, A1.M4_-, A1.CH3_-, A1.CH2_-, A1.CH1_-, F1.GND, A2.Pin_2, A2.Pin_3, Grove1.GND, M2.pin2, M3.pin2, A5.Pin_1, Adaptor_12V.NEG, R1.Pin_1, DHT2.Gnd, R3.Pin_0, F2.GND, Part2.L/R, Part2.GND, S1.Pin_1, S1.Pin_2
  N1: M1.IO35, R4.Pin_0
  N2: M1.IO36, R1.Pin_0, R2.pin_1
  N3: M1.IO26, A1.CH1_S
  N4: M1.IO25, A1.CH2_S
  N5: M1.IO17, A1.CH3_S
  N6: M1.IO16, DHT2.Signal
  N7: M1.IO14, S1.Pin_3, S1.Pin_4
  N8: M1.IO13, Part2.SD
  N9: M1.IO5, M3.pin1
  N10: M1.IO23, M2.pin1
  N11: M1.IO19, Part2.WS
  N12: M1.IO18, Part2.SCK
  N13: M1.SDA, Grove1.SDA
  N14: M1.SCL, Grove1.SCL
  N15: Part1.1, Adaptor_12V.POS
  N16: Part1.2, Part1.OUT, A1.M1_+, R5.Pin_0
  N17: A1.M2_+, A2.Pin_1
  5V_2: A1.M3_+, F1.5V, F2.5V
  N18: A1.M4_+, A5.Pin_2

custom parts:
  >Wemos D1 R32: Wemos D1 R32 - This board is used with dual-mode Wi-Fi and Bluetooth chips, which is safe, reliable, and scalable to a variety of applications. DC in 5V-12V, 1 analog input(3.2V max input), a Micro USB connection, Compatible with D1 R32=WiFi+bluetooth+UNO
  four channel mosfet switch: Four Channel 4 Route MOSFET Button IRF540 V4.0+ MOSFET Switch Module for (4way).
  Fan - Ventilador: Ventilador de 2 pines, se encuentra comunmente en computadoras de escritorio
  COB 12V LED strip: 12V flexible COB LED strip.
  100w-ptc-air-heater: 110V 100W Surface Insulated PTC Air Heater PTC Heating Element Incubator Controller Incubation Heater.
  DHT11 Humitidy and Temperature Sensor (3 pins): DHT11 Humidity and Temperature Sensor (3 pins).
  INMP441: This is a simple breakout board for the INMP441 I2S MEMS microphone.
